// Logisim project KinematicController.circ as structural Verilog: 3 circuits, main circuit kinematic_controller
module reflect (
  input  [2:0] in_1,
  output [2:0] out_2
);

  wire and_1_out, and_2_out, clock_1_out, comparator_1_eq, comparator_2_eq, comparator_3_eq, comparator_4_eq,
       not_1_out, not_4_out, not_5_out, or_1_out;
  wire [1:0] random_1_out;
  wire [2:0] adder_1_out, adder_2_out, demultiplexer_1_out0, demultiplexer_1_out1, divider_1_out,
       divider_2_rem, not_2_out, not_3_out, random_2_out, register_1_q, subtractor_1_out, transistor_1_out,
       transistor_3_out;

  // Probe on in_1
  Comparator #(.width(3)) comparator_1 (.a(in_1), .b(3'b100), .eq(comparator_1_eq));  // open: gt, lt
  // Probe on comparator_1_eq
  Register #(.width(3)) register_1 (.D(in_1), .Q(register_1_q), .clk(clock_1_out));  // open: en, clr
  Clock #(.lowDuration(10)) clock_1 (.out(clock_1_out));
  Demultiplexer #(.width(3)) demultiplexer_1 (
    .out0(demultiplexer_1_out0), .out1(demultiplexer_1_out1), .in(in_1), .sel(comparator_1_eq));  // open: en
  not not_1 (not_1_out, comparator_2_eq);
  Comparator #(.width(3)) comparator_2 (.a(register_1_q), .b(in_1), .eq(comparator_2_eq));  // open: gt, lt
  // Probe on demultiplexer_1_out0
  // Probe on demultiplexer_1_out1
  Transistor #(.\type ("n"), .width(3)) transistor_1 (.in(not_2_out), .out(transistor_1_out), .gate(comparator_1_eq));
  assign not_2_out = ~demultiplexer_1_out1;  // NOT_Gate not_2, 3 bits wide
  assign not_3_out = ~demultiplexer_1_out0;  // NOT_Gate not_3, 3 bits wide
  Adder #(.width(3)) adder_1 (.a(not_3_out), .b(3'b001), .out(adder_1_out));  // open: cin, cout
  Transistor #(.width(3)) transistor_2 (.in(adder_1_out), .out(transistor_1_out), .gate(comparator_1_eq));
  Random #(.width(2)) random_1 (.clk(not_1_out), .next(not_1_out), .out(random_1_out));  // open: clr
  Random #(.width(3), .seed(1234)) random_2 (.clk(not_1_out), .next(not_1_out), .out(random_2_out));  // open: clr
  and and_1 (and_1_out, random_1_out[0], random_1_out[1]);
  and and_2 (and_2_out, and_1_out, not_4_out);
  Divider #(.width(3)) divider_1 (.a(3'b011), .b(3'b010), .out(divider_1_out));  // open: upper, rem
  Divider #(.width(3)) divider_2 (.a(random_2_out), .b(3'b011), .rem(divider_2_rem));  // open: out, upper
  Subtractor #(.width(3)) subtractor_1 (
    .a(divider_2_rem), .b(divider_1_out), .out(subtractor_1_out));  // open: bin, bout
  Adder #(.width(3)) adder_2 (.a(subtractor_1_out), .b(transistor_1_out), .out(adder_2_out));  // open: cin, cout
  // Probe on subtractor_1_out
  // Probe on transistor_1_out
  Comparator #(.width(3)) comparator_3 (.a(adder_2_out), .b(3'b000), .eq(comparator_3_eq));  // open: gt, lt
  Comparator #(.width(3)) comparator_4 (.a(adder_2_out), .b(3'b100), .eq(comparator_4_eq));  // open: gt, lt
  not not_4 (not_4_out, or_1_out);
  or or_1 (or_1_out, comparator_3_eq, comparator_4_eq);
  not not_5 (not_5_out, and_2_out);
  Transistor #(.width(3)) transistor_3 (.in(subtractor_1_out), .out(transistor_3_out), .gate(not_5_out));
  Transistor #(.width(3)) transistor_4 (.in(3'b000), .out(transistor_3_out), .gate(and_2_out));
  Adder #(.width(3)) adder_3 (.a(transistor_3_out), .b(transistor_1_out), .out(out_2));  // open: cin, cout
  // Probe on out_2
endmodule

module inrange (
  input  [4:0] Yball,
  input  [4:0] Ybat,
  output out_3
);

  wire comparator_1_eq, comparator_2_eq, comparator_3_eq;
  wire [4:0] adder_1_out, adder_2_out;

  Comparator #(.width(5)) comparator_1 (.a(Yball), .b(Ybat), .eq(comparator_1_eq));  // open: gt, lt
  Adder #(.width(5)) adder_1 (.a(Ybat), .b(5'b00001), .out(adder_1_out));  // open: cin, cout
  Adder #(.width(5)) adder_2 (.a(Ybat), .b(5'b00010), .out(adder_2_out));  // open: cin, cout
  Comparator #(.width(5)) comparator_2 (.a(Yball), .b(adder_1_out), .eq(comparator_2_eq));  // open: gt, lt
  Comparator #(.width(5)) comparator_3 (.a(Yball), .b(adder_2_out), .eq(comparator_3_eq));  // open: gt, lt
  or or_1 (out_3, comparator_1_eq, comparator_2_eq, comparator_3_eq);
endmodule

module kinematic_controller (
  input  [4:0] outbot,
  input  [4:0] LXin,
  input  [4:0] LYin,
  input  Reset,
  input  Tact,
  output [7:0] VX,
  output [7:0] X,
  output [7:0] VY,
  output [4:0] RYout,
  output [7:0] Y,
  output [4:0] LXout,
  output [4:0] ballX,
  output [4:0] ballY,
  output [7:0] RXin,
  output [4:0] RXout,
  output [4:0] LYout,
  output [7:0] Rs,
  output [7:0] Ls,
  output LossSignal
);

  wire adder_3_cout, adder_4_cout, adder_5_cout, adder_6_cout, adder_9_cout, adder_10_cout, and_1_out,
       and_2_out, and_3_out, Bcontact, clock_1_out, clock_2_out, comparator_1_gt, comparator_1_lt,
       comparator_2_gt, comparator_2_lt, comparator_3_eq, comparator_3_gt, comparator_4_eq, comparator_4_gt,
       comparator_5_gt, comparator_5_lt, comparator_6_gt, comparator_6_lt, comparator_7_gt, comparator_8_gt,
       comparator_8_lt, comparator_9_eq, comparator_9_gt, comparator_9_lt, comparator_10_eq,
       comparator_10_lt, hitA, hitB, inrange_1_out_3, inrange_2_out_3, LBcontact, not_1_out, not_2_out,
       not_3_out, not_4_out, not_5_out, not_6_out, not_7_out, not_8_out, or_1_out, or_2_out, or_3_out,
       or_6_out, or_9_out, or_10_out, RBcontact, subtractor_5_bout, subtractor_6_bout, transistor_14_out,
       vxneg, vyneg, xrefl, yrefl;
  wire [2:0] adder_5_out, bit_extender_8_out, leftXin, multiplexer_1_out, multiplexer_2_out,
       multiplexer_5_out, negator_1_out, random_1_out, reflect_1_out_2, subtractor_2_out, subtractor_5_out,
       transistor_1_out, transistor_3_out, vx_t, vy_t;
  wire [4:0] adder_6_out, adder_11_out, adder_13_out, adder_14_out, bit_extender_9_out, bit_extender_11_out,
       counter_3_q, multiplexer_6_out, register_5_q, register_6_q, shifter_5_out, shifter_6_out,
       subtractor_3_out, subtractor_6_out, transistor_5_out, transistor_7_out, transistor_9_out,
       transistor_11_out;
  wire [7:0] adder_1_out, adder_2_out, adder_7_out, adder_8_out, adder_12_out, bit_extender_7_out,
       bit_extender_12_out, multiplexer_3_out, multiplexer_4_out, shifter_1_out, shifter_2_out,
       shifter_3_out, shifter_4_out, shifter_7_out, shifter_8_out, subtractor_1_out, subtractor_4_out;

  // Probe on vx_t
  reflect reflect_1 (.in_1(vy_t), .out_2(reflect_1_out_2));
  // Probe on negator_1_out
  Negator #(.width(3)) negator_1 (.in(vx_t), .out(negator_1_out));
  Multiplexer #(.width(3), .disabled(0)) multiplexer_1 (
    .in0(negator_1_out), .in1(3'b110), .out(multiplexer_1_out), .sel(Reset));  // open: en
  or or_1 (or_1_out, xrefl, Bcontact, Reset);
  Multiplexer #(.width(3)) multiplexer_2 (
    .in0(reflect_1_out_2), .in1(3'b001), .out(multiplexer_2_out), .sel(Reset));  // open: en
  or or_2 (or_2_out, yrefl, Reset);
  not not_1 (not_1_out, xrefl);
  and and_1 (and_1_out, not_1_out, not_2_out);
  not not_2 (not_2_out, Bcontact);
  // Probe on multiplexer_1_out
  // Probe on multiplexer_2_out
  Adder adder_1 (.a(X), .b(VX), .out(adder_1_out));  // open: cin, cout
  Multiplexer #(.width(8)) multiplexer_3 (
    .in0(adder_1_out), .in1(8'hc0), .out(multiplexer_3_out), .sel(Reset));  // open: en
  or or_3 (or_3_out, and_1_out, Reset);
  // Probe on vx_t
  Register #(.width(3)) u_vx (.D(multiplexer_1_out), .en(or_1_out), .Q(vx_t), .clk(Tact));  // open: clr
  Register #(.width(3), .trigger("falling")) u_vy (
    .D(multiplexer_2_out), .en(or_2_out), .Q(vy_t), .clk(Tact));  // open: clr
  // Probe on vy_t
  Register #(.trigger("falling")) xreg (.D(multiplexer_3_out), .en(or_3_out), .Q(X), .clk(Tact));  // open: clr
  not not_3 (not_3_out, Bcontact);
  Shifter #(.shift("lr")) shifter_1 (.in(X), .\dist (3'b011), .out(shifter_1_out));
  Bit_Extender #(.out_width(5)) bit_extender_1 (.in(shifter_1_out), .out(ballX));
  or or_4 (Bcontact, LBcontact, RBcontact);
  and and_2 (and_2_out, hitA, not_3_out);
  or or_5 (LossSignal, and_2_out, and_3_out);
  and and_3 (and_3_out, not_3_out, hitB);
  assign VX = {{5{vx_t[2]}}, vx_t};  // Bit_Extender bit_extender_2
  assign VY = {{5{vy_t[2]}}, vy_t};  // Bit_Extender bit_extender_3
  Adder adder_2 (.a(Y), .b(VY), .out(adder_2_out));  // open: cin, cout
  not not_4 (not_4_out, xrefl);
  // Probe on X
  // Probe on VX
  Shifter #(.shift("lr")) shifter_2 (.in(VX), .\dist (3'b111), .out(shifter_2_out));
  Bit_Extender #(.out_width(1)) bit_extender_4 (.in(shifter_2_out), .out(vxneg));
  Multiplexer #(.width(8)) multiplexer_4 (
    .in0(adder_2_out), .in1(8'h80), .out(multiplexer_4_out), .sel(Reset));  // open: en
  Register yreg (.D(multiplexer_4_out), .en(or_6_out), .Q(Y), .clk(Tact));  // open: clr
  or or_6 (or_6_out, not_4_out, Reset);
  Adder adder_3 (.a(X), .b(VX), .cout(adder_3_cout));  // open: out, cin
  // Probe on vxneg
  Shifter #(.shift("lr")) shifter_3 (.in(Y), .\dist (3'b011), .out(shifter_3_out));
  Counter counter_1 (.D(8'h1), .count(hitA), .Q(Rs), .clk(Tact), .clr(Reset));  // open: load, carry
  Comparator #(.width(1)) comparator_1 (
    .a(adder_3_cout), .b(vxneg), .gt(comparator_1_gt), .lt(comparator_1_lt));  // open: eq
  // Probe on vyneg
  Bit_Extender #(.out_width(1)) bit_extender_5 (.in(shifter_4_out), .out(vyneg));
  Shifter #(.shift("lr")) shifter_4 (.in(VY), .\dist (3'b111), .out(shifter_4_out));
  Adder adder_4 (.a(VY), .b(Y), .cout(adder_4_cout));  // open: out, cin
  Bit_Extender #(.out_width(5)) bit_extender_6 (.in(shifter_3_out), .out(ballY));
  Counter counter_2 (.D(8'h1), .count(hitB), .Q(Ls), .clk(Tact), .clr(Reset));  // open: load, carry
  not not_5 (not_5_out, vxneg);
  or or_7 (xrefl, comparator_1_gt, comparator_1_lt);
  // Probe on hitB
  and and_4 (hitB, not_5_out, xrefl);
  and and_5 (hitA, vxneg, xrefl);
  // Probe on hitA
  or or_8 (yrefl, comparator_2_gt, comparator_2_lt);
  Comparator #(.width(1)) comparator_2 (
    .a(vyneg), .b(adder_4_cout), .gt(comparator_2_gt), .lt(comparator_2_lt));  // open: eq
  Comparator #(.width(5), .mode("unsigned")) comparator_3 (
    .a(LXin), .b(5'b10000), .gt(comparator_3_gt), .eq(comparator_3_eq));  // open: lt
  Comparator #(.width(5), .mode("unsigned")) comparator_4 (
    .a(LYin), .b(5'b01111), .gt(comparator_4_gt), .eq(comparator_4_eq));  // open: lt
  assign bit_extender_7_out = {{5{1'b0}}, leftXin};  // Bit_Extender bit_extender_7
  Bit_Extender #(.in_width(5), .out_width(3)) bit_extender_8 (.in(shifter_5_out), .out(bit_extender_8_out));
  Shifter #(.width(5), .shift("lr")) shifter_5 (.in(LXin), .\dist (3'b100), .out(shifter_5_out));
  Shifter #(.width(5), .shift("lr")) shifter_6 (.in(LYin), .\dist (3'b100), .out(shifter_6_out));
  Subtractor subtractor_1 (.a({8{1'b1}}), .b(RXin), .out(subtractor_1_out));  // open: bin, bout
  Shifter shifter_7 (.in(bit_extender_7_out), .\dist (3'b011), .out(shifter_7_out));
  Subtractor #(.width(3)) subtractor_2 (.a(3'b001), .b(bit_extender_8_out), .out(subtractor_2_out));  // open: bin, bout
  Subtractor #(.width(5)) subtractor_3 (.a(5'b00001), .b(shifter_6_out), .out(subtractor_3_out));  // open: bin, bout
  // Probe on subtractor_1_out
  // Probe on subtractor_4_out
  Subtractor subtractor_4 (.a(8'hfb), .b(shifter_7_out), .out(subtractor_4_out));  // open: bin, bout
  Subtractor #(.width(3)) subtractor_5 (
    .a(leftXin), .b(subtractor_2_out), .out(subtractor_5_out), .bout(subtractor_5_bout));  // open: bin
  Adder #(.width(3)) adder_5 (
    .a(bit_extender_8_out), .b(leftXin), .out(adder_5_out), .cout(adder_5_cout));  // open: cin
  Subtractor #(.width(5)) subtractor_6 (
    .a(LYout), .b(subtractor_3_out), .out(subtractor_6_out), .bout(subtractor_6_bout));  // open: bin
  Adder #(.width(5)) adder_6 (.a(shifter_6_out), .b(LYout), .out(adder_6_out), .cout(adder_6_cout));  // open: cin
  Adder adder_7 (.a(X), .b(subtractor_1_out), .out(adder_7_out));  // open: cin, cout
  Adder adder_8 (.a(X), .b(subtractor_4_out), .out(adder_8_out));  // open: cin, cout
  Transistor #(.gate("br"), .width(3)) transistor_1 (
    .in(multiplexer_5_out), .out(transistor_1_out), .gate(subtractor_5_bout));
  Multiplexer #(.width(3)) multiplexer_5 (
    .in0(subtractor_5_out), .in1(adder_5_out), .out(multiplexer_5_out), .sel(comparator_3_gt));  // open: en
  Transistor #(.\type ("n"), .width(3)) transistor_2 (.in(3'b000), .out(transistor_1_out), .gate(subtractor_5_bout));
  Multiplexer #(.width(5)) multiplexer_6 (
    .in0(subtractor_6_out), .in1(adder_6_out), .out(multiplexer_6_out), .sel(comparator_4_gt));  // open: en
  Adder adder_9 (.a(VX), .b(adder_7_out), .cout(adder_9_cout));  // open: out, cin
  Comparator #(.width(1)) comparator_5 (
    .a(adder_9_cout), .b(vxneg), .gt(comparator_5_gt), .lt(comparator_5_lt));  // open: eq
  Adder adder_10 (.a(VX), .b(adder_8_out), .cout(adder_10_cout));  // open: out, cin
  Comparator #(.width(1)) comparator_6 (
    .a(adder_10_cout), .b(vxneg), .gt(comparator_6_gt), .lt(comparator_6_lt));  // open: eq
  Transistor #(.gate("br"), .width(3)) transistor_3 (
    .in(transistor_1_out), .out(transistor_3_out), .gate(adder_5_cout));
  Transistor #(.\type ("n"), .width(3)) transistor_4 (.in(3'b111), .out(transistor_3_out), .gate(adder_5_cout));
  Transistor #(.gate("br"), .width(5)) transistor_5 (
    .in(multiplexer_6_out), .out(transistor_5_out), .gate(subtractor_6_bout));
  Transistor #(.\type ("n"), .width(5)) transistor_6 (.in({5{1'b0}}), .out(transistor_5_out), .gate(subtractor_6_bout));
  or or_9 (or_9_out, comparator_5_gt, comparator_5_lt);
  inrange inrange_1 (.Yball(ballY), .Ybat(RYout), .out_3(inrange_1_out_3));
  or or_10 (or_10_out, comparator_6_gt, comparator_6_lt);
  inrange inrange_2 (.Yball(ballY), .Ybat(LYout), .out_3(inrange_2_out_3));
  assign bit_extender_9_out = {{2{1'b0}}, transistor_3_out};  // Bit_Extender bit_extender_9
  Transistor #(.gate("br"), .width(5)) transistor_7 (
    .in(transistor_5_out), .out(transistor_7_out), .gate(adder_6_cout));
  not not_6 (not_6_out, comparator_4_eq);
  Transistor #(.\type ("n"), .width(5)) transistor_8 (.in(5'b11101), .out(transistor_7_out), .gate(adder_6_cout));
  and and_6 (RBcontact, or_9_out, inrange_1_out_3);
  and and_7 (LBcontact, or_10_out, inrange_2_out_3);
  Register #(.width(5), .trigger("falling")) register_1 (
    .D(bit_extender_9_out), .en(not_7_out), .Q(LXout), .clk(clock_1_out));  // open: clr
  not not_7 (not_7_out, comparator_3_eq);
  Clock #(.highDuration(4), .lowDuration(4)) clock_1 (.out(clock_1_out));
  Register #(.width(5), .trigger("falling")) register_2 (
    .D(transistor_7_out), .en(not_6_out), .Q(LYout), .clk(clock_2_out));  // open: clr
  Clock #(.highDuration(4), .lowDuration(4)) clock_2 (.out(clock_2_out));
  Bit_Extender #(.in_width(5), .out_width(3)) bit_extender_10 (.in(LXout), .out(leftXin));
  Random #(.width(3)) random_1 (.clk(comparator_7_gt), .next(comparator_7_gt), .out(random_1_out));  // open: clr
  Comparator #(.mode("unsigned")) comparator_7 (.a(8'h80), .b(VX), .gt(comparator_7_gt));  // open: eq, lt
  assign bit_extender_11_out = {{2{1'b0}}, random_1_out};  // Bit_Extender bit_extender_11
  Adder #(.width(5)) adder_11 (.a(bit_extender_11_out), .b(5'b11000), .out(adder_11_out));  // open: cin, cout
  assign bit_extender_12_out = {{3{1'b0}}, adder_11_out};  // Bit_Extender bit_extender_12
  Comparator #(.width(5), .mode("unsigned")) comparator_8 (
    .a(outbot), .b(5'b11110), .gt(comparator_8_gt), .eq(comparator_8_gt), .lt(comparator_8_lt));
  Transistor #(.\type ("n"), .width(5)) transistor_9 (.in(5'b11101), .out(transistor_9_out), .gate(comparator_8_gt));
  Transistor #(.\type ("n"), .width(5)) transistor_10 (.in(outbot), .out(transistor_9_out), .gate(comparator_8_lt));
  Shifter shifter_8 (.in(bit_extender_12_out), .\dist (3'b011), .out(shifter_8_out));
  Adder adder_12 (.a(shifter_8_out), .b(8'h3), .out(adder_12_out));  // open: cin, cout
  Register register_3 (.D(adder_12_out), .en(comparator_7_gt), .Q(RXin), .clk(Tact));  // open: clr
  Comparator #(.width(5), .mode("unsigned")) comparator_9 (
    .a(RYout), .b(transistor_9_out), .gt(comparator_9_gt), .eq(comparator_9_eq), .lt(comparator_9_lt));
  Transistor #(.\type ("n"), .width(5)) transistor_11 (
    .in(adder_13_out), .out(transistor_11_out), .gate(comparator_9_lt));
  Adder #(.width(5)) adder_13 (.a(RYout), .b(5'b00001), .out(adder_13_out));  // open: cin, cout
  Adder #(.width(5)) adder_14 (.a(RYout), .b({5{1'b1}}), .out(adder_14_out));  // open: cin, cout
  // Probe on RXin
  Transistor #(.\type ("n"), .width(5)) transistor_12 (
    .in(adder_14_out), .out(transistor_11_out), .gate(comparator_9_gt));
  Transistor #(.\type ("n"), .width(5)) transistor_13 (.in(RYout), .out(transistor_11_out), .gate(comparator_9_eq));
  Register #(.width(5), .trigger("falling")) register_4 (
    .D(transistor_11_out), .Q(RYout), .clk(Tact));  // open: en, clr
  Register #(.width(5)) register_5 (.D(adder_11_out), .en(comparator_7_gt), .Q(register_5_q), .clk(Tact));  // open: clr
  Register #(.width(5)) register_6 (.D(register_5_q), .en(comparator_7_gt), .Q(register_6_q), .clk(Tact));  // open: clr
  Comparator #(.width(5), .mode("unsigned")) comparator_10 (
    .a(register_5_q), .b(register_6_q), .eq(comparator_10_eq), .lt(comparator_10_lt));  // open: gt
  not not_8 (not_8_out, comparator_10_eq);
  Counter #(.width(5), .max('h1f)) counter_3 (
    .load(comparator_10_lt), .D(5'b00001), .count(transistor_14_out), .Q(counter_3_q), .clk(Tact),
    .clr(comparator_7_gt));  // open: carry
  Transistor #(.gate("br")) transistor_14 (.in(1'b0), .out(transistor_14_out), .gate(not_8_out));
  Transistor transistor_15 (.in(Tact), .out(transistor_14_out), .gate(comparator_10_eq));
  Adder #(.width(5)) adder_15 (.a(counter_3_q), .b(register_6_q), .out(RXout));  // open: cin, cout

  // Other names for the same wires on the sheet: leftYin[4:0] = LYout; longVX[7:0] = VX; longVY[7:0] = VY;
  //   Rbatx[7:0] = RXin; rightYin[4:0] = RYout; xreg[7:0] = X; yreg[7:0] = Y

  // Notes on the sheet:
  //   Reset: pull=down
  //   LossSignal: pull=down
  //   Other
  //   Counting the X ball
  //   Hitting the ball against the wall
  //   Counting the Y ball
  //   Score
  //   Contact with left/right bat
  //   Moving Player's bat
  //   Moving Computer's bat
endmodule
