// Logisim project Processor.circ as structural Verilog: 1 circuit, main circuit Processor
module Processor (
  input  [7:0] X,
  input  [7:0] Y,
  input  [7:0] VX,
  input  [7:0] VY,
  input  [7:0] batX,
  output [4:0] OUT
);

  wire cdm_8_mark5_1_data_inst, cdm_8_mark5_1_mem_cycle, clock_1_out, decoder_1_out0, decoder_1_out1,
       IO_3_2_out, IO_3_3_out, IO_3_4_out, IO_3_5_out, IO_3_out, IOsel, not_1_out, READwrite;
  wire [3:0] cdm_8_mark5_1_ps, IOaddr;
  wire [7:0] cdm_8_mark5_1_data_out, cdm_8_mark5_1_pc, cdm_8_mark5_1_r0, cdm_8_mark5_1_r1, cdm_8_mark5_1_r2,
       cdm_8_mark5_1_r3, cdm_8_mark5_1_sp, controlled_buffer_4_out, IOdat, shifter_1_out;
  wire [7:4] cdm_8_mark5_1_addr;

  Shifter #(.shift("lr")) shifter_1 (.in(cdm_8_mark5_1_r0), .\dist (3'b011), .out(shifter_1_out));
  Bit_Extender #(.out_width(5)) bit_extender_1 (.in(shifter_1_out), .out(OUT));
  // Probe on IOdat
  assign IOdat = IO_3_out ? X : 8'bz;  // Controlled_Buffer controlled_buffer_1
  // Probe on cdm_8_mark5_1_r3
  // Probe on cdm_8_mark5_1_r2
  // Probe on cdm_8_mark5_1_r1
  Clock clock_1 (.out(clock_1_out));
  and IO_3 (IO_3_out, READwrite, IOsel, IOaddr[0], IOaddr[1], ~IOaddr[2], ~IOaddr[3]);  // AND_Gate
  assign IOdat = IO_3_2_out ? Y : 8'bz;  // Controlled_Buffer controlled_buffer_2
  and and_1 (IOsel, cdm_8_mark5_1_addr[4], cdm_8_mark5_1_addr[5], cdm_8_mark5_1_addr[6], cdm_8_mark5_1_addr[7], decoder_1_out1);
  // Probe on cdm_8_mark5_1_ps
  // Probe on cdm_8_mark5_1_pc
  // Probe on cdm_8_mark5_1_sp
  CdM_8_mark5 cdm_8_mark5_1 (
    .clock(clock_1_out), .addr({cdm_8_mark5_1_addr, IOaddr}), .mem_read(READwrite),
    .mem_cycle(cdm_8_mark5_1_mem_cycle), .data_inst(cdm_8_mark5_1_data_inst),
    .data_out(cdm_8_mark5_1_data_out), .data_in(controlled_buffer_4_out), .r0(cdm_8_mark5_1_r0),
    .r1(cdm_8_mark5_1_r1), .r2(cdm_8_mark5_1_r2), .r3(cdm_8_mark5_1_r3), .PC(cdm_8_mark5_1_pc),
    .SP(cdm_8_mark5_1_sp), .PS(cdm_8_mark5_1_ps));
  Decoder #(.disabled(0)) decoder_1 (
    .out0(decoder_1_out0), .out1(decoder_1_out1), .sel(cdm_8_mark5_1_data_inst), .en(cdm_8_mark5_1_mem_cycle));
  not not_1 (not_1_out, READwrite);
  assign IOdat = not_1_out ? cdm_8_mark5_1_data_out : 8'bz;  // Controlled_Buffer controlled_buffer_3
  assign controlled_buffer_4_out = READwrite ? IOdat : 8'bz;  // Controlled_Buffer controlled_buffer_4
  and IO_3_2 (IO_3_2_out, READwrite, IOsel, ~IOaddr[0], ~IOaddr[1], IOaddr[2], ~IOaddr[3]);  // AND_Gate
  assign IOdat = IO_3_3_out ? VX : 8'bz;  // Controlled_Buffer controlled_buffer_5
  // Probe on {cdm_8_mark5_1_addr, IOaddr}
  and IO_3_3 (IO_3_3_out, READwrite, IOsel, IOaddr[0], ~IOaddr[1], IOaddr[2], ~IOaddr[3]);  // AND_Gate
  assign IOdat = IO_3_4_out ? VY : 8'bz;  // Controlled_Buffer controlled_buffer_6
  ROM rom_1 (.addr({cdm_8_mark5_1_addr, IOaddr}), .data(IOdat), .sel(decoder_1_out0));
  // Probe on IOdat
  and IO_3_4 (IO_3_4_out, READwrite, IOsel, ~IOaddr[0], IOaddr[1], IOaddr[2], ~IOaddr[3]);  // AND_Gate
  assign IOdat = IO_3_5_out ? batX : 8'bz;  // Controlled_Buffer controlled_buffer_7
  // Probe on IOdat
  and IO_3_5 (IO_3_5_out, READwrite, IOsel, IOaddr[0], IOaddr[1], IOaddr[2], ~IOaddr[3]);  // AND_Gate

  // Notes on the sheet:
  //   contents of rom_1 (hex, n*v repeats v):
  //   d2 f6 ba d3 1 3b f e1 1b d2 f4 ba d1 f3 b5 d3 f7 bf 3d 99 16 e3 1a d3 ff 3e 8 d3 2 3b f e1 32 d2 f4
  //   ba d1 f3 b5 d3 f7 bf 3d 16 e3 31 d3 ff 3e 8 d3 3 3b f e1 54 d2 f4 ba d1 f3 b5 d3 f7 bf 3d 7 99 1d e3
  //   4d 16 d3 ff 3e ee 53 16 e3 53 d3 ff 3e 8 d3 1 1b f e1 6b d2 f4 ba d1 f3 b5 d3 f7 bf 3d 99 39 5 e5 6a
  //   85 4 d3 2 1b f e1 81 d2 f4 ba d1 f3 b5 d3 f7 bf 3d 39 5 e5 80 85 4 d3 3 1b f e1 9a d2 f4 ba d1 f3 b5
  //   d3 f7 bf 3d 7 99 39 37 f e5 99 87 c ee
endmodule
