// Logisim project VideoSubsystem.circ as structural Verilog: 3 circuits, main circuit Chip1x32
module Chip1x32 (
  input  [4:0] BallX,
  input  [4:0] BallY,
  input  [4:0] LBatX,
  input  [4:0] LBatY,
  input  [4:0] RBatX,
  input  [4:0] RBatY,
  input  [4:0] ChipID,
  input  Tact,
  output [31:0] M,
  output [4:0] BallX_out,
  output [4:0] BallY_out,
  output [4:0] LBatX_out,
  output [4:0] LBatY_out,
  output [4:0] RBatX_out,
  output [4:0] RBatY_out,
  output [4:0] ChipID_2,
  output Tact_2
);

  wire comparator_1_eq, comparator_2_eq, comparator_3_eq;
  wire [4:0] demultiplexer_1_out1, demultiplexer_2_out1, demultiplexer_3_out1;
  wire [31:0] demultiplexer_4_out0, demultiplexer_4_out1, multiplexer_1_out, multiplexer_2_out,
       multiplexer_3_out, not_1_out, or_1_out, shifter_1_out, shifter_2_out, shifter_3_out;

  Comparator #(.width(5)) comparator_1 (.a(BallX), .b(ChipID), .eq(comparator_1_eq));  // open: gt, lt
  // Probe on comparator_1_eq
  Demultiplexer #(.width(5), .tristate("true")) demultiplexer_1 (
    .out1(demultiplexer_1_out1), .in(BallY), .sel(comparator_1_eq));  // open: out0, en
  // Probe on comparator_2_eq
  Comparator #(.width(5)) comparator_2 (.a(LBatX), .b(ChipID), .eq(comparator_2_eq));  // open: gt, lt
  Demultiplexer #(.width(5), .tristate("true")) demultiplexer_2 (
    .out1(demultiplexer_2_out1), .in(LBatY), .sel(comparator_2_eq));  // open: out0, en
  // Probe on comparator_3_eq
  Comparator #(.width(5)) comparator_3 (.a(RBatX), .b(ChipID), .eq(comparator_3_eq));  // open: gt, lt
  Demultiplexer #(.width(5), .tristate("true")) demultiplexer_3 (
    .out1(demultiplexer_3_out1), .in(RBatY), .sel(comparator_3_eq));  // open: out0, en
  // Probe on demultiplexer_1_out1
  // Probe on demultiplexer_2_out1
  // Probe on demultiplexer_3_out1
  Shifter #(.width(32)) shifter_1 (.in(32'h1), .\dist (demultiplexer_1_out1), .out(shifter_1_out));
  Shifter #(.width(32)) shifter_2 (.in(32'h7), .\dist (demultiplexer_2_out1), .out(shifter_2_out));
  Shifter #(.width(32)) shifter_3 (.in(32'h7), .\dist (demultiplexer_3_out1), .out(shifter_3_out));
  Multiplexer #(.width(32)) multiplexer_1 (
    .in0({32{1'b0}}), .in1(shifter_1_out), .out(multiplexer_1_out), .sel(comparator_1_eq));  // open: en
  Multiplexer #(.width(32)) multiplexer_2 (
    .in0({32{1'b0}}), .in1(shifter_2_out), .out(multiplexer_2_out), .sel(comparator_2_eq));  // open: en
  Multiplexer #(.width(32)) multiplexer_3 (
    .in0({32{1'b0}}), .in1(shifter_3_out), .out(multiplexer_3_out), .sel(comparator_3_eq));  // open: en
  // Probe on multiplexer_1_out
  // Probe on multiplexer_2_out
  // Probe on multiplexer_3_out
  Multiplexer #(.width(32)) multiplexer_4 (
    .in0(demultiplexer_4_out0), .in1(not_1_out), .out(M), .sel(Tact));  // open: en
  assign not_1_out = ~demultiplexer_4_out1;  // NOT_Gate not_1, 32 bits wide
  Demultiplexer #(.width(32), .disabled(0)) demultiplexer_4 (
    .out0(demultiplexer_4_out0), .out1(demultiplexer_4_out1), .in(or_1_out), .sel(Tact), .en(1'b1));
  assign or_1_out = multiplexer_1_out | multiplexer_2_out | multiplexer_3_out;  // OR_Gate or_1, 32 bits wide
  Adder #(.width(5)) adder_1 (.a(ChipID), .b(5'b00001), .out(ChipID_2));  // open: cin, cout

  assign BallX_out = BallX;
  assign BallY_out = BallY;
  assign LBatX_out = LBatX;
  assign LBatY_out = LBatY;
  assign RBatX_out = RBatX;
  assign RBatY_out = RBatY;
  assign Tact_2 = Tact;

  // Notes on the sheet:
  //   In
  //   Matrix Input
  //   Out
endmodule

module \Chip8х32  (
  input  [4:0] BallX,
  input  [4:0] BallY,
  input  [4:0] LBatX,
  input  [4:0] LBatY,
  input  [4:0] RBatX,
  input  [4:0] RBatY,
  input  Tact,
  input  [4:0] ChipID,
  output [31:0] out_9,
  output [31:0] out_10,
  output [31:0] out_11,
  output [31:0] out_12,
  output [31:0] out_13,
  output [31:0] out_14,
  output [31:0] out_15,
  output [31:0] out_16,
  output [4:0] BallX_2,
  output [4:0] BallY_2,
  output [4:0] LBatX_2,
  output [4:0] LBatY_2,
  output [4:0] RBatX_2,
  output [4:0] RBatY_2,
  output Tact_2,
  output [4:0] ChipID_2
);

  wire chip1x32_1_tact_2, chip1x32_2_tact_2, chip1x32_3_tact_2, chip1x32_4_tact_2, chip1x32_5_tact_2,
       chip1x32_6_tact_2, chip1x32_7_tact_2;
  wire [4:0] chip1x32_1_ballx_out, chip1x32_1_bally_out, chip1x32_1_chipid_2, chip1x32_1_lbatx_out,
       chip1x32_1_lbaty_out, chip1x32_1_rbatx_out, chip1x32_1_rbaty_out, chip1x32_2_ballx_out,
       chip1x32_2_bally_out, chip1x32_2_chipid_2, chip1x32_2_lbatx_out, chip1x32_2_lbaty_out,
       chip1x32_2_rbatx_out, chip1x32_2_rbaty_out, chip1x32_3_ballx_out, chip1x32_3_bally_out,
       chip1x32_3_chipid_2, chip1x32_3_lbatx_out, chip1x32_3_lbaty_out, chip1x32_3_rbatx_out,
       chip1x32_3_rbaty_out, chip1x32_4_ballx_out, chip1x32_4_bally_out, chip1x32_4_chipid_2,
       chip1x32_4_lbatx_out, chip1x32_4_lbaty_out, chip1x32_4_rbatx_out, chip1x32_4_rbaty_out,
       chip1x32_5_ballx_out, chip1x32_5_bally_out, chip1x32_5_chipid_2, chip1x32_5_lbatx_out,
       chip1x32_5_lbaty_out, chip1x32_5_rbatx_out, chip1x32_5_rbaty_out, chip1x32_6_ballx_out,
       chip1x32_6_bally_out, chip1x32_6_chipid_2, chip1x32_6_lbatx_out, chip1x32_6_lbaty_out,
       chip1x32_6_rbatx_out, chip1x32_6_rbaty_out, chip1x32_7_ballx_out, chip1x32_7_bally_out,
       chip1x32_7_chipid_2, chip1x32_7_lbatx_out, chip1x32_7_lbaty_out, chip1x32_7_rbatx_out,
       chip1x32_7_rbaty_out;

  Chip1x32 chip1x32_1 (
    .BallX(BallX), .BallY(BallY), .LBatX(LBatX), .LBatY(LBatY), .RBatX(RBatX), .RBatY(RBatY),
    .ChipID(ChipID), .BallX_out(chip1x32_1_ballx_out), .BallY_out(chip1x32_1_bally_out),
    .LBatX_out(chip1x32_1_lbatx_out), .LBatY_out(chip1x32_1_lbaty_out), .RBatX_out(chip1x32_1_rbatx_out),
    .RBatY_out(chip1x32_1_rbaty_out), .ChipID_2(chip1x32_1_chipid_2), .M(out_9), .Tact(Tact),
    .Tact_2(chip1x32_1_tact_2));
  Chip1x32 chip1x32_2 (
    .BallX(chip1x32_1_ballx_out), .BallY(chip1x32_1_bally_out), .LBatX(chip1x32_1_lbatx_out),
    .LBatY(chip1x32_1_lbaty_out), .RBatX(chip1x32_1_rbatx_out), .RBatY(chip1x32_1_rbaty_out),
    .ChipID(chip1x32_1_chipid_2), .BallX_out(chip1x32_2_ballx_out), .BallY_out(chip1x32_2_bally_out),
    .LBatX_out(chip1x32_2_lbatx_out), .LBatY_out(chip1x32_2_lbaty_out), .RBatX_out(chip1x32_2_rbatx_out),
    .RBatY_out(chip1x32_2_rbaty_out), .ChipID_2(chip1x32_2_chipid_2), .M(out_10), .Tact(chip1x32_1_tact_2),
    .Tact_2(chip1x32_2_tact_2));
  Chip1x32 chip1x32_3 (
    .BallX(chip1x32_2_ballx_out), .BallY(chip1x32_2_bally_out), .LBatX(chip1x32_2_lbatx_out),
    .LBatY(chip1x32_2_lbaty_out), .RBatX(chip1x32_2_rbatx_out), .RBatY(chip1x32_2_rbaty_out),
    .ChipID(chip1x32_2_chipid_2), .BallX_out(chip1x32_3_ballx_out), .BallY_out(chip1x32_3_bally_out),
    .LBatX_out(chip1x32_3_lbatx_out), .LBatY_out(chip1x32_3_lbaty_out), .RBatX_out(chip1x32_3_rbatx_out),
    .RBatY_out(chip1x32_3_rbaty_out), .ChipID_2(chip1x32_3_chipid_2), .M(out_11), .Tact(chip1x32_2_tact_2),
    .Tact_2(chip1x32_3_tact_2));
  Chip1x32 chip1x32_4 (
    .BallX(chip1x32_3_ballx_out), .BallY(chip1x32_3_bally_out), .LBatX(chip1x32_3_lbatx_out),
    .LBatY(chip1x32_3_lbaty_out), .RBatX(chip1x32_3_rbatx_out), .RBatY(chip1x32_3_rbaty_out),
    .ChipID(chip1x32_3_chipid_2), .BallX_out(chip1x32_4_ballx_out), .BallY_out(chip1x32_4_bally_out),
    .LBatX_out(chip1x32_4_lbatx_out), .LBatY_out(chip1x32_4_lbaty_out), .RBatX_out(chip1x32_4_rbatx_out),
    .RBatY_out(chip1x32_4_rbaty_out), .ChipID_2(chip1x32_4_chipid_2), .M(out_12), .Tact(chip1x32_3_tact_2),
    .Tact_2(chip1x32_4_tact_2));
  Chip1x32 chip1x32_5 (
    .BallX(chip1x32_4_ballx_out), .BallY(chip1x32_4_bally_out), .LBatX(chip1x32_4_lbatx_out),
    .LBatY(chip1x32_4_lbaty_out), .RBatX(chip1x32_4_rbatx_out), .RBatY(chip1x32_4_rbaty_out),
    .ChipID(chip1x32_4_chipid_2), .BallX_out(chip1x32_5_ballx_out), .BallY_out(chip1x32_5_bally_out),
    .LBatX_out(chip1x32_5_lbatx_out), .LBatY_out(chip1x32_5_lbaty_out), .RBatX_out(chip1x32_5_rbatx_out),
    .RBatY_out(chip1x32_5_rbaty_out), .ChipID_2(chip1x32_5_chipid_2), .M(out_13), .Tact(chip1x32_4_tact_2),
    .Tact_2(chip1x32_5_tact_2));
  Chip1x32 chip1x32_6 (
    .BallX(chip1x32_5_ballx_out), .BallY(chip1x32_5_bally_out), .LBatX(chip1x32_5_lbatx_out),
    .LBatY(chip1x32_5_lbaty_out), .RBatX(chip1x32_5_rbatx_out), .RBatY(chip1x32_5_rbaty_out),
    .ChipID(chip1x32_5_chipid_2), .BallX_out(chip1x32_6_ballx_out), .BallY_out(chip1x32_6_bally_out),
    .LBatX_out(chip1x32_6_lbatx_out), .LBatY_out(chip1x32_6_lbaty_out), .RBatX_out(chip1x32_6_rbatx_out),
    .RBatY_out(chip1x32_6_rbaty_out), .ChipID_2(chip1x32_6_chipid_2), .M(out_14), .Tact(chip1x32_5_tact_2),
    .Tact_2(chip1x32_6_tact_2));
  Chip1x32 chip1x32_7 (
    .BallX(chip1x32_6_ballx_out), .BallY(chip1x32_6_bally_out), .LBatX(chip1x32_6_lbatx_out),
    .LBatY(chip1x32_6_lbaty_out), .RBatX(chip1x32_6_rbatx_out), .RBatY(chip1x32_6_rbaty_out),
    .ChipID(chip1x32_6_chipid_2), .BallX_out(chip1x32_7_ballx_out), .BallY_out(chip1x32_7_bally_out),
    .LBatX_out(chip1x32_7_lbatx_out), .LBatY_out(chip1x32_7_lbaty_out), .RBatX_out(chip1x32_7_rbatx_out),
    .RBatY_out(chip1x32_7_rbaty_out), .ChipID_2(chip1x32_7_chipid_2), .M(out_15), .Tact(chip1x32_6_tact_2),
    .Tact_2(chip1x32_7_tact_2));
  Chip1x32 chip1x32_8 (
    .BallX(chip1x32_7_ballx_out), .BallY(chip1x32_7_bally_out), .LBatX(chip1x32_7_lbatx_out),
    .LBatY(chip1x32_7_lbaty_out), .RBatX(chip1x32_7_rbatx_out), .RBatY(chip1x32_7_rbaty_out),
    .ChipID(chip1x32_7_chipid_2), .BallX_out(BallX_2), .BallY_out(BallY_2), .LBatX_out(LBatX_2),
    .LBatY_out(LBatY_2), .RBatX_out(RBatX_2), .RBatY_out(RBatY_2), .ChipID_2(ChipID_2), .M(out_16),
    .Tact(chip1x32_7_tact_2), .Tact_2(Tact_2));
endmodule

module Video_subsystem (
  input  Signal,
  input  [4:0] BallX,
  input  [4:0] BallY,
  input  [4:0] LBatX,
  input  [4:0] LBatY,
  input  [4:0] RBatX,
  input  [4:0] RBatY,
  output Tact,
  output [31:0] out_9,
  output [31:0] out_10,
  output [31:0] out_11,
  output [31:0] out_12,
  output [31:0] out_13,
  output [31:0] out_14,
  output [31:0] out_15,
  output [31:0] out_16,
  output [31:0] out_17,
  output [31:0] out_18,
  output [31:0] out_19,
  output [31:0] out_20,
  output [31:0] out_21,
  output [31:0] out_22,
  output [31:0] out_23,
  output [31:0] out_24,
  output [31:0] out_25,
  output [31:0] out_26,
  output [31:0] out_27,
  output [31:0] out_28,
  output [31:0] out_29,
  output [31:0] out_30,
  output [31:0] out_31,
  output [31:0] out_32,
  output [31:0] out_33,
  output [31:0] out_34,
  output [31:0] out_35,
  output [31:0] out_36,
  output [31:0] out_37,
  output [31:0] out_38,
  output [31:0] out_39,
  output [31:0] out_40
);

  wire \chip8х32_1_tact_2 , \chip8х32_2_tact_2 , \chip8х32_3_tact_2 , clock_1_out, clock_2_out,
       counter_1_carry, counter_2_q, demultiplexer_1_out1, not_1_out, transistor_1_out;
  wire [4:0] \chip8х32_1_ballx_2 , \chip8х32_1_bally_2 , \chip8х32_1_chipid_2 , \chip8х32_1_lbatx_2 ,
       \chip8х32_1_lbaty_2 , \chip8х32_1_rbatx_2 , \chip8х32_1_rbaty_2 , \chip8х32_2_ballx_2 ,
       \chip8х32_2_bally_2 , \chip8х32_2_chipid_2 , \chip8х32_2_lbatx_2 , \chip8х32_2_lbaty_2 ,
       \chip8х32_2_rbatx_2 , \chip8х32_2_rbaty_2 , \chip8х32_3_ballx_2 , \chip8х32_3_bally_2 ,
       \chip8х32_3_chipid_2 , \chip8х32_3_lbatx_2 , \chip8х32_3_lbaty_2 , \chip8х32_3_rbatx_2 ,
       \chip8х32_3_rbaty_2 ;

  not not_1 (not_1_out, counter_2_q);
  Clock #(.highDuration(20), .lowDuration(20)) clock_1 (.out(clock_1_out));
  Clock #(.highDuration(2), .lowDuration(2)) clock_2 (.out(clock_2_out));
  Demultiplexer #(.disabled(0)) demultiplexer_1 (
    .out0(Tact), .out1(demultiplexer_1_out1), .in(clock_2_out), .sel(counter_2_q), .en(1'b1));
  Transistor transistor_1 (.in(1'b0), .out(transistor_1_out), .gate(counter_2_q));
  Transistor transistor_2 (.in(clock_1_out), .out(transistor_1_out), .gate(not_1_out));
  Counter #(.width(5), .max('h1f)) counter_1 (
    .D(5'b00001), .count(demultiplexer_1_out1), .carry(counter_1_carry), .clk(demultiplexer_1_out1),
    .clr(counter_1_carry));  // open: load, Q
  \Chip8х32  \chip8х32_1  (
    .BallX(BallX), .BallY(BallY), .LBatX(LBatX), .LBatY(LBatY), .RBatX(RBatX), .RBatY(RBatY),
    .ChipID({5{1'b0}}), .BallX_2(\chip8х32_1_ballx_2 ), .BallY_2(\chip8х32_1_bally_2 ),
    .LBatX_2(\chip8х32_1_lbatx_2 ), .LBatY_2(\chip8х32_1_lbaty_2 ), .RBatX_2(\chip8х32_1_rbatx_2 ),
    .RBatY_2(\chip8х32_1_rbaty_2 ), .ChipID_2(\chip8х32_1_chipid_2 ), .out_9(out_9), .out_10(out_10),
    .out_11(out_11), .out_12(out_12), .out_13(out_13), .out_14(out_14), .out_15(out_15), .out_16(out_16),
    .Tact(transistor_1_out), .Tact_2(\chip8х32_1_tact_2 ));
  \Chip8х32  \chip8х32_2  (
    .BallX(\chip8х32_1_ballx_2 ), .BallY(\chip8х32_1_bally_2 ), .LBatX(\chip8х32_1_lbatx_2 ),
    .LBatY(\chip8х32_1_lbaty_2 ), .RBatX(\chip8х32_1_rbatx_2 ), .RBatY(\chip8х32_1_rbaty_2 ),
    .ChipID(\chip8х32_1_chipid_2 ), .BallX_2(\chip8х32_2_ballx_2 ), .BallY_2(\chip8х32_2_bally_2 ),
    .LBatX_2(\chip8х32_2_lbatx_2 ), .LBatY_2(\chip8х32_2_lbaty_2 ), .RBatX_2(\chip8х32_2_rbatx_2 ),
    .RBatY_2(\chip8х32_2_rbaty_2 ), .ChipID_2(\chip8х32_2_chipid_2 ), .out_9(out_17), .out_10(out_18),
    .out_11(out_19), .out_12(out_20), .out_13(out_21), .out_14(out_22), .out_15(out_23), .out_16(out_24),
    .Tact(\chip8х32_1_tact_2 ), .Tact_2(\chip8х32_2_tact_2 ));
  \Chip8х32  \chip8х32_3  (
    .BallX(\chip8х32_2_ballx_2 ), .BallY(\chip8х32_2_bally_2 ), .LBatX(\chip8х32_2_lbatx_2 ),
    .LBatY(\chip8х32_2_lbaty_2 ), .RBatX(\chip8х32_2_rbatx_2 ), .RBatY(\chip8х32_2_rbaty_2 ),
    .ChipID(\chip8х32_2_chipid_2 ), .BallX_2(\chip8х32_3_ballx_2 ), .BallY_2(\chip8х32_3_bally_2 ),
    .LBatX_2(\chip8х32_3_lbatx_2 ), .LBatY_2(\chip8х32_3_lbaty_2 ), .RBatX_2(\chip8х32_3_rbatx_2 ),
    .RBatY_2(\chip8х32_3_rbaty_2 ), .ChipID_2(\chip8х32_3_chipid_2 ), .out_9(out_25), .out_10(out_26),
    .out_11(out_27), .out_12(out_28), .out_13(out_29), .out_14(out_30), .out_15(out_31), .out_16(out_32),
    .Tact(\chip8х32_2_tact_2 ), .Tact_2(\chip8х32_3_tact_2 ));
  \Chip8х32  \chip8х32_4  (
    .BallX(\chip8х32_3_ballx_2 ), .BallY(\chip8х32_3_bally_2 ), .LBatX(\chip8х32_3_lbatx_2 ),
    .LBatY(\chip8х32_3_lbaty_2 ), .RBatX(\chip8х32_3_rbatx_2 ), .RBatY(\chip8х32_3_rbaty_2 ),
    .ChipID(\chip8х32_3_chipid_2 ), .out_9(out_33), .out_10(out_34), .out_11(out_35), .out_12(out_36),
    .out_13(out_37), .out_14(out_38), .out_15(out_39), .out_16(out_40), .Tact(\chip8х32_3_tact_2 ));  // open: BallX_2, BallY_2, LBatX_2, LBatY_2, RBatX_2, RBatY_2, ChipID_2, Tact_2
  Counter #(.width(1), .max('h1)) counter_2 (
    .D(1'b1), .count(Signal), .Q(counter_2_q), .clk(Signal), .clr(counter_1_carry));  // open: load, carry

  // Notes on the sheet:
  //   Signal: pull=down
  //   Tact: pull=down
endmodule
