// Logisim project main.circ as structural Verilog: 2 circuits, main circuit main
module main (
);

  wire kinematic_controller_1_losssignal, R_out, video_subsystem_1_tact;
  wire [3:0] score_1_fstdigit, score_1_snddigit, score_2_fstdigit, score_2_snddigit;
  wire [4:0] joystick_1_x, joystick_1_y, kinematic_controller_1_ballx, kinematic_controller_1_bally,
       kinematic_controller_1_lxout, kinematic_controller_1_lyout, kinematic_controller_1_rxout,
       kinematic_controller_1_ryout, not_1_out, processor_1_out;
  wire [7:0] kinematic_controller_1_rxin, kinematic_controller_1_vx, kinematic_controller_1_vy,
       kinematic_controller_1_x, kinematic_controller_1_y, Ls, Rs;
  wire [31:0] video_subsystem_1_out_9, video_subsystem_1_out_10, video_subsystem_1_out_11,
       video_subsystem_1_out_12, video_subsystem_1_out_13, video_subsystem_1_out_14,
       video_subsystem_1_out_15, video_subsystem_1_out_16, video_subsystem_1_out_17,
       video_subsystem_1_out_18, video_subsystem_1_out_19, video_subsystem_1_out_20,
       video_subsystem_1_out_21, video_subsystem_1_out_22, video_subsystem_1_out_23,
       video_subsystem_1_out_24, video_subsystem_1_out_25, video_subsystem_1_out_26,
       video_subsystem_1_out_27, video_subsystem_1_out_28, video_subsystem_1_out_29,
       video_subsystem_1_out_30, video_subsystem_1_out_31, video_subsystem_1_out_32,
       video_subsystem_1_out_33, video_subsystem_1_out_34, video_subsystem_1_out_35,
       video_subsystem_1_out_36, video_subsystem_1_out_37, video_subsystem_1_out_38,
       video_subsystem_1_out_39, video_subsystem_1_out_40;

  Hex_Digit_Display hex_digit_display_1 (.value(score_1_fstdigit));  // open: dp
  Hex_Digit_Display hex_digit_display_2 (.value(score_1_snddigit));  // open: dp
  score score_1 (.FstDigit(score_1_fstdigit), .SndDigit(score_1_snddigit), .Score(Ls));
  Joystick #(.bits(5)) joystick_1 (.x(joystick_1_x), .y(joystick_1_y));
  Button R (.out(R_out));
  assign not_1_out = ~joystick_1_y;  // NOT_Gate not_1, 5 bits wide
  Processor processor_1 (
    .X(kinematic_controller_1_x), .Y(kinematic_controller_1_y), .VX(kinematic_controller_1_vx),
    .VY(kinematic_controller_1_vy), .OUT(processor_1_out), .batX(kinematic_controller_1_rxin));
  DotMatrix #(.matrixcols(32), .matrixrows(32)) dotmatrix_1 (
    .col0(video_subsystem_1_out_9), .col1(video_subsystem_1_out_10), .col2(video_subsystem_1_out_11),
    .col3(video_subsystem_1_out_12), .col4(video_subsystem_1_out_13), .col5(video_subsystem_1_out_14),
    .col6(video_subsystem_1_out_15), .col7(video_subsystem_1_out_16), .col8(video_subsystem_1_out_17),
    .col9(video_subsystem_1_out_18), .col10(video_subsystem_1_out_19), .col11(video_subsystem_1_out_20),
    .col12(video_subsystem_1_out_21), .col13(video_subsystem_1_out_22), .col14(video_subsystem_1_out_23),
    .col15(video_subsystem_1_out_24), .col16(video_subsystem_1_out_25), .col17(video_subsystem_1_out_26),
    .col18(video_subsystem_1_out_27), .col19(video_subsystem_1_out_28), .col20(video_subsystem_1_out_29),
    .col21(video_subsystem_1_out_30), .col22(video_subsystem_1_out_31), .col23(video_subsystem_1_out_32),
    .col24(video_subsystem_1_out_33), .col25(video_subsystem_1_out_34), .col26(video_subsystem_1_out_35),
    .col27(video_subsystem_1_out_36), .col28(video_subsystem_1_out_37), .col29(video_subsystem_1_out_38),
    .col30(video_subsystem_1_out_39), .col31(video_subsystem_1_out_40));
  kinematic_controller kinematic_controller_1 (
    .LYout(kinematic_controller_1_lyout), .LYin(not_1_out), .Ls(Ls), .Rs(Rs), .Tact(video_subsystem_1_tact),
    .LXin(joystick_1_x), .LXout(kinematic_controller_1_lxout), .RYout(kinematic_controller_1_ryout),
    .outbot(processor_1_out), .X(kinematic_controller_1_x), .VY(kinematic_controller_1_vy),
    .VX(kinematic_controller_1_vx), .LossSignal(kinematic_controller_1_losssignal), .Reset(R_out),
    .ballX(kinematic_controller_1_ballx), .ballY(kinematic_controller_1_bally), .Y(kinematic_controller_1_y),
    .RXout(kinematic_controller_1_rxout), .RXin(kinematic_controller_1_rxin));
  Video_subsystem video_subsystem_1 (
    .RBatX(kinematic_controller_1_rxout), .RBatY(kinematic_controller_1_ryout),
    .Tact(video_subsystem_1_tact), .Signal(kinematic_controller_1_losssignal),
    .BallX(kinematic_controller_1_ballx), .BallY(kinematic_controller_1_bally),
    .LBatX(kinematic_controller_1_lxout), .LBatY(kinematic_controller_1_lyout),
    .out_9(video_subsystem_1_out_9), .out_10(video_subsystem_1_out_10), .out_11(video_subsystem_1_out_11),
    .out_12(video_subsystem_1_out_12), .out_13(video_subsystem_1_out_13), .out_14(video_subsystem_1_out_14),
    .out_15(video_subsystem_1_out_15), .out_16(video_subsystem_1_out_16), .out_17(video_subsystem_1_out_17),
    .out_18(video_subsystem_1_out_18), .out_19(video_subsystem_1_out_19), .out_20(video_subsystem_1_out_20),
    .out_21(video_subsystem_1_out_21), .out_22(video_subsystem_1_out_22), .out_23(video_subsystem_1_out_23),
    .out_24(video_subsystem_1_out_24), .out_25(video_subsystem_1_out_25), .out_26(video_subsystem_1_out_26),
    .out_27(video_subsystem_1_out_27), .out_28(video_subsystem_1_out_28), .out_29(video_subsystem_1_out_29),
    .out_30(video_subsystem_1_out_30), .out_31(video_subsystem_1_out_31), .out_32(video_subsystem_1_out_32),
    .out_33(video_subsystem_1_out_33), .out_34(video_subsystem_1_out_34), .out_35(video_subsystem_1_out_35),
    .out_36(video_subsystem_1_out_36), .out_37(video_subsystem_1_out_37), .out_38(video_subsystem_1_out_38),
    .out_39(video_subsystem_1_out_39), .out_40(video_subsystem_1_out_40));
  Hex_Digit_Display hex_digit_display_3 (.value(score_2_fstdigit));  // open: dp
  Hex_Digit_Display hex_digit_display_4 (.value(score_2_snddigit));  // open: dp
  score score_2 (.FstDigit(score_2_fstdigit), .SndDigit(score_2_snddigit), .Score(Rs));
endmodule

module score (
  input  [7:0] Score,
  output [3:0] FstDigit,
  output [3:0] SndDigit
);

  wire [7:0] divider_1_out, divider_1_rem;

  // Probe on FstDigit
  // Probe on Score
  // Probe on SndDigit
  Bit_Extender #(.out_width(4)) bit_extender_1 (.in(divider_1_out), .out(FstDigit));
  Divider divider_1 (.a(Score), .b(8'ha), .out(divider_1_out), .rem(divider_1_rem));  // open: upper
  Bit_Extender #(.out_width(4)) bit_extender_2 (.in(divider_1_rem), .out(SndDigit));
endmodule
